# Fritzing sketch schematics (saved by Fritzing 0.7.7b)
breadboards: 1

parts:
  Arduino1 = Arduino
  LED1 = LED - 5mm [color="Green (570nm)" package="5 mm [THT]"]
  LED2 = LED - 5mm [color="Green (570nm)" package="5 mm [THT]"]
  LED3 = LED - 5mm [color="Green (570nm)" package="5 mm [THT]"]
  LED5 = LED - 5mm [color="Green (570nm)" package="5 mm [THT]"]
  R1 = Resistor [tolerance=±5% resistance=220 package="0603 [SMD]"]
  R2 = Resistor [tolerance=±5% resistance=220 package="0603 [SMD]"]
  R3 = Resistor [tolerance=±5% resistance=220 package="0603 [SMD]"]
  R4 = Resistor [tolerance=±5% resistance=220 package="0603 [SMD]"]
  R5 = Resistor [tolerance=±5% resistance=220 package="0603 [SMD]"]
  Button = Pushbutton [package="[THT]"]
  R6 = Resistor [tolerance=±5% resistance=10k package="0603 [SMD]"]
  LED4 = LED - 5mm [color="Green (570nm)" package="5 mm [THT]"]
  J1 = Infrared Proximity Sensor

nets:
  N1: Arduino1.D13, LED1.anode
  N2: Arduino1.D12, LED2.anode
  N3: Arduino1.D11, LED3.anode
  N4: Arduino1.D10, LED4.anode
  N5: Arduino1.D9, LED5.anode
  N6: Arduino1.D8, Button.Pin_3, Button.Pin_4, R6.Pin_1
  +5V: Arduino1.+5V, Button.Pin_1, Button.Pin_2, J1.Vcc
  GND: Arduino1.GND, R1.Pin_0, R3.Pin_0, R4.Pin_0, R6.Pin_0, J1.GND
  N7: Arduino1.A0, J1.Vout
  N8: LED1.cathode, R1.Pin_1
  N9: LED2.cathode, R2.Pin_1
  N10: LED3.cathode, R3.Pin_1
  N11: LED5.cathode, R5.Pin_1
  N12: R4.Pin_1, LED4.cathode
