# Fritzing sketch schematics (saved by Fritzing 0.7.7b)
breadboards: 1

parts:
  Arduino1 = Arduino
  J2 = Basic Servo
  J3 = Basic Servo
  J1 = Infrared Proximity Sensor

nets:
  N1: Arduino1.D7, J2.pulse
  N2: Arduino1.D4, J3.pulse
  VCC: Arduino1.+5V, J2.vcc, J3.vcc, J1.Vcc
  GND: Arduino1.GND, J2.gnd, J3.gnd, J1.GND
  N3: Arduino1.A0, J1.Vout
